# Fritzing sketch LED01 (saved by Fritzing 0.9.3b)
breadboards: 1

parts:
  U1 = NodeMCU V1.0
  LED1 = LED - 5mm [color="Red (633nm)" package="5 mm [THT]"]
  R1 = Resistor [tolerance=±5% resistance=220 package=THT]

nets:
  N1: U1.D2, R1.Pin_1
  N2: U1.GND, LED1.cathode
  N3: LED1.anode, R1.Pin_0

custom parts:
  NodeMCU V1.0: ESP8266 based NodeMCU
