# Fritzing sketch LED02 (saved by Fritzing 0.9.3b)
breadboards: 1

parts:
  U1 = NodeMCU V1.0
  LED1 = LED - 5mm [color="Red (633nm)" package="5 mm [THT]"]
  R1 = Resistor [tolerance=±5% resistance=220 package=THT]
  LED2 = LED - 5mm [color="Yellow (595nm)" package="5 mm [THT]"]
  R2 = Resistor [tolerance=±5% resistance=220 package=THT]

nets:
  N1: U1.D1, R1.Pin_1
  N2: U1.D2, R2.Pin_1
  N3: U1.GND, LED1.cathode, LED2.cathode
  N4: LED1.anode, R1.Pin_0
  N5: LED2.anode, R2.Pin_0

custom parts:
  NodeMCU V1.0: ESP8266 based NodeMCU
