# Fritzing sketch LED03 (saved by Fritzing 0.9.3b)
breadboards: 1

parts:
  U1 = NodeMCU V1.0
  LED1 = LED - 5mm [color="Red (633nm)" package="5 mm [THT]"]
  R1 = Resistor [tolerance=±5% resistance=220 package=THT]
  LED2 = LED - 5mm [color="Yellow (595nm)" package="5 mm [THT]"]
  R2 = Resistor [tolerance=±5% resistance=220 package=THT]
  LED3 = LED - 5mm [color="Blue (525nm)" package="5 mm [THT]"]
  R3 = Resistor [tolerance=±5% resistance=220 package=THT]

nets:
  N1: U1.D2, R1.Pin_1
  N2: U1.D4, R2.Pin_1
  N3: U1.GND, LED1.cathode, LED2.cathode, LED3.cathode
  N4: U1.D6, R3.Pin_1
  N5: LED1.anode, R1.Pin_0
  N6: LED2.anode, R2.Pin_0
  N7: LED3.anode, R3.Pin_0

custom parts:
  NodeMCU V1.0: ESP8266 based NodeMCU
